// Logisim project cpu.circ as structural Verilog: 32 circuits, main circuit Main
module Main (
  input  in_1,
  input  in_2
);

  wire and_1_out, clock_1_out, cu_1_coclk, cu_1_csclk, cu_1_dsclk, cu_1_erclk, cu_1_erclr, cu_1_frclk,
       cu_1_killclk, cu_1_out_42, cu_1_rst, cu_1_ssclk, cu_1_wri, demultiplexer_1_out1, demultiplexer_1_out2,
       demultiplexer_1_out3, demultiplexer_1_out4, demultiplexer_1_out5, demultiplexer_2_out0,
       demultiplexer_2_out1, demultiplexer_2_out2, demultiplexer_2_out3, demultiplexer_2_out4,
       demultiplexer_2_out5, demultiplexer_2_out6, not_1_out, or_1_out, or_2_out, or_3_out,
       parallel_out_2402ca5c_1_clk, parallel_out_2402ca5c_1_reset;
  wire [1:0] cu_1_er, ER_q;
  wire [2:0] counter_1_out_3, cu_1_reg;
  wire [4:0] IR_q;
  wire [5:0] cu_1_overflow;
  wire [7:0] adder_1_out, AX_q, BX_q, CO_q, cu_1_coin, cu_1_csin, cu_1_dsin, cu_1_out, cu_1_ssin, CX_q, DS_q,
       DX_q, dx_select_360570a6_1_dx, FR_q, multiplexer_1_out, network_in_65bb84dc_1_out,
       parallel_out_2402ca5c_1_data, PC_q, RA_q, RB_q, SS_q;
  wire [15:0] multiplexer_2_out;
  wire [20:0] cu_1_out_43, ram_1_dout, WR_q;

  Clock clock_1 (.out(clock_1_out));
  Counter counter_1 (.Clock(clock_1_out), .Clear(or_1_out), .out_3(counter_1_out_3));
  or or_1 (or_1_out, in_1, cu_1_rst);
  Demultiplexer #(.select(3)) demultiplexer_1 (
    .out1(demultiplexer_1_out1), .out2(demultiplexer_1_out2), .out3(demultiplexer_1_out3),
    .out4(demultiplexer_1_out4), .out5(demultiplexer_1_out5), .in(1'b1), .sel(counter_1_out_3));  // open: out0, out6, out7
  Adder adder_1 (.a(PC_q), .b(8'h1), .out(adder_1_out));  // open: cin, cout
  or or_2 (or_2_out, demultiplexer_1_out3, demultiplexer_1_out4, demultiplexer_1_out5);
  Multiplexer #(.width(8)) multiplexer_1 (.in0(adder_1_out), .in1(cu_1_csin), .out(multiplexer_1_out), .sel(or_2_out));
  Register CO (.D(cu_1_coin), .Q(CO_q), .clk(cu_1_coclk), .clr(cu_1_rst));  // open: en
  Register PC (.D(multiplexer_1_out), .Q(PC_q), .clk(cu_1_csclk), .clr(cu_1_rst));  // open: en
  Register DS (.D(cu_1_dsin), .Q(DS_q), .clk(cu_1_dsclk), .clr(cu_1_rst));  // open: en
  Register SS (.D(cu_1_ssin), .Q(SS_q), .clk(cu_1_ssclk), .clr(cu_1_rst));  // open: en
  RAM #(.addrWidth(16), .dataWidth(21), .enables("line")) ram_1 (
    .addr(multiplexer_2_out), .we(cu_1_wri), .clk(cu_1_wri), .din(cu_1_out_43), .dout(ram_1_dout));
  Register #(.width(2)) ER (.D(cu_1_er), .Q(ER_q), .clk(cu_1_erclk), .clr(or_3_out));  // open: en
  or or_3 (or_3_out, cu_1_rst, cu_1_erclr);
  Multiplexer #(.select(2), .width(16)) multiplexer_2 (
    .in0({CO_q, PC_q}), .in1({8'hfe, DS_q}), .in2({{8{1'b1}}, SS_q}), .out(multiplexer_2_out), .sel(ER_q));  // open: in3
  Register #(.width(21)) WR (.D(ram_1_dout), .Q(WR_q), .clk(demultiplexer_1_out1), .clr(cu_1_rst));  // open: en
  Register RB (.D(WR_q[7:0]), .Q(RB_q), .clk(demultiplexer_1_out2), .clr(cu_1_rst));  // open: en
  Register RA (.D(WR_q[15:8]), .Q(RA_q), .clk(demultiplexer_1_out2), .clr(cu_1_rst));  // open: en
  Register #(.width(5)) IR (.D(WR_q[20:16]), .Q(IR_q), .clk(demultiplexer_1_out2), .clr(cu_1_rst));  // open: en
  CU cu_1 (
    .IR(IR_q), .RA(RA_q), .RB(RB_q), .AX(AX_q), .BX(BX_q), .CX(CX_q), .DX(DX_q), .CO(CO_q), .CS(PC_q),
    .DS(DS_q), .SS(SS_q), .Data(ram_1_dout), .in_17(FR_q[5]), .EQ(FR_q[4]), .in_19(FR_q[3]), .ZF(FR_q[1]),
    .KillCLK(cu_1_killclk), .Overflow(cu_1_overflow[0]), .FRCLK(cu_1_frclk), .CSCLK(cu_1_csclk),
    .COCLK(cu_1_coclk), .DSCLK(cu_1_dsclk), .SSCLK(cu_1_ssclk), .ERCLK(cu_1_erclk), .WRI(cu_1_wri),
    .Decode(demultiplexer_1_out2), .Execute(demultiplexer_1_out3), .Store(demultiplexer_1_out4),
    .Clear(demultiplexer_1_out5), .CSCLKSTORMUX5(demultiplexer_2_out4), .COCLKSTORMUX4(demultiplexer_2_out5),
    .CSCLKSTORMUX6(demultiplexer_2_out6), .ERCLR(cu_1_erclr), .CSIn(cu_1_csin), .DSIn(cu_1_dsin),
    .ER(cu_1_er), .Out(cu_1_out), .Reg(cu_1_reg), .GT(cu_1_overflow[5]), .out_40(cu_1_overflow[4]),
    .LT(cu_1_overflow[3]), .out_42(cu_1_out_42), .out_43(cu_1_out_43), .RST(cu_1_rst), .SSIn(cu_1_ssin),
    .COIn(cu_1_coin));
  and and_1 (and_1_out, demultiplexer_1_out4, not_1_out);
  not not_1 (not_1_out, cu_1_killclk);
  Demultiplexer #(.select(3)) demultiplexer_2 (
    .out0(demultiplexer_2_out0), .out1(demultiplexer_2_out1), .out2(demultiplexer_2_out2),
    .out3(demultiplexer_2_out3), .out4(demultiplexer_2_out4), .out5(demultiplexer_2_out5),
    .out6(demultiplexer_2_out6), .in(and_1_out), .sel(cu_1_reg));  // open: out7
  Register AX (.D(cu_1_out), .Q(AX_q), .clk(demultiplexer_2_out0), .clr(cu_1_out_42));  // open: en
  // Probe on demultiplexer_2_out0
  // Probe on demultiplexer_2_out1
  ZeroFlag zeroflag_1 (.in_1(AX_q), .out_2(cu_1_overflow[1]));
  Register BX (.D(cu_1_out), .Q(BX_q), .clk(demultiplexer_2_out1), .clr(cu_1_out_42));  // open: en
  // Probe on demultiplexer_2_out2
  Register CX (.D(cu_1_out), .Q(CX_q), .clk(demultiplexer_2_out2), .clr(cu_1_out_42));  // open: en
  // Probe on demultiplexer_2_out3
  DX_SELECT_360570a6 dx_select_360570a6_1 (
    .CU(cu_1_out), .BX(BX_q), .DX(dx_select_360570a6_1_dx), .NW(network_in_65bb84dc_1_out));
  Register FR (
    .D({{2{in_2}}, cu_1_overflow[5:3], in_2, cu_1_overflow[1:0]}), .Q(FR_q), .clk(cu_1_frclk));  // open: en, clr
  Register DX (.D(dx_select_360570a6_1_dx), .Q(DX_q), .clk(demultiplexer_2_out3), .clr(cu_1_out_42));  // open: en
  NETWORK_IN_65bb84dc network_in_65bb84dc_1 (.NETWORK_CTRL_15d682f0(CX_q), .OUT(network_in_65bb84dc_1_out));
  PARALLEL_OUT_2402ca5c parallel_out_2402ca5c_1 (
    .D(DX_q), .CTRL(CX_q), .Data(parallel_out_2402ca5c_1_data), .CLK(parallel_out_2402ca5c_1_clk),
    .RESET(parallel_out_2402ca5c_1_reset));
  TTY tty_1 (
    .data(parallel_out_2402ca5c_1_data[6:0]), .clk(parallel_out_2402ca5c_1_clk),
    .clr(parallel_out_2402ca5c_1_reset));  // open: we

  // Notes on the sheet:
  //   Clock
  //   ZF
endmodule

module Add (
  input  [7:0] RA,
  input  Cin,
  input  [7:0] AX,
  input  [7:0] BX,
  input  [7:0] CX,
  input  [7:0] DX,
  output Overflow,
  output [7:0] Out
);

  wire [7:0] multiplexer_1_out;

  Multiplexer #(.select(2), .width(8)) multiplexer_1 (
    .in0(AX), .in1(BX), .in2(CX), .in3(DX), .out(multiplexer_1_out), .sel(RA[1:0]));
  Adder adder_1 (.a(AX), .b(multiplexer_1_out), .out(Out), .cin(Cin), .cout(Overflow));
endmodule

module Sub (
  input  [7:0] RA,
  input  Cin,
  input  [7:0] AX,
  input  [7:0] BX,
  input  [7:0] CX,
  input  [7:0] DX,
  output Overflow,
  output [7:0] Out
);

  wire [7:0] multiplexer_1_out;

  Multiplexer #(.select(2), .width(8)) multiplexer_1 (
    .in0(AX), .in1(BX), .in2(CX), .in3(DX), .out(multiplexer_1_out), .sel(RA[1:0]));
  Subtractor subtractor_1 (.a(AX), .b(multiplexer_1_out), .out(Out), .bin(Cin), .bout(Overflow));
endmodule

module ZeroFlag (
  input  [7:0] in_1,
  output out_2
);

  wire or_1_out, or_2_out;

  or or_1 (or_1_out, in_1[0], in_1[1], in_1[2], in_1[3], in_1[4]);
  or or_2 (or_2_out, in_1[5], in_1[6], in_1[7]);
  nor nor_1 (out_2, or_1_out, or_2_out);
endmodule

module Mult (
  input  [7:0] RA,
  input  [7:0] AX,
  input  [7:0] BX,
  input  [7:0] CX,
  input  [7:0] DX,
  output Overflow,
  output [7:0] Out
);

  wire zeroflag_1_out_2;
  wire [7:0] multiplexer_1_out, multiplier_1_cout;

  Multiplexer #(.select(2), .width(8)) multiplexer_1 (
    .in0(AX), .in1(BX), .in2(CX), .in3(DX), .out(multiplexer_1_out), .sel(RA[1:0]));
  Multiplier multiplier_1 (.a(AX), .b(multiplexer_1_out), .out(Out), .cout(multiplier_1_cout));  // open: cin
  not not_1 (Overflow, zeroflag_1_out_2);
  ZeroFlag zeroflag_1 (.in_1(multiplier_1_cout), .out_2(zeroflag_1_out_2));

  // Notes on the sheet:
  //   ZF
endmodule

module ALU (
  input  [7:0] AX,
  input  [7:0] BX,
  input  [7:0] CX,
  input  [7:0] DX,
  input  [7:0] RA,
  input  [4:0] IR,
  output Overflow,
  output [7:0] Out,
  output [2:0] Reg
);

  wire add_1_overflow, mult_1_overflow, sub_1_overflow;
  wire [7:0] add_1_out, div2_1_out, mult_1_out, sub_1_out;

  Mult mult_1 (.RA(RA), .AX(AX), .BX(BX), .CX(CX), .DX(DX), .Overflow(mult_1_overflow), .Out(mult_1_out));
  Sub sub_1 (.RA(RA), .AX(AX), .BX(BX), .CX(CX), .DX(DX), .Overflow(sub_1_overflow), .Out(sub_1_out));  // open: Cin
  Add add_1 (.RA(RA), .AX(AX), .BX(BX), .CX(CX), .DX(DX), .Overflow(add_1_overflow), .Out(add_1_out));  // open: Cin
  DIV2 div2_1 (.RA(RA), .AX(AX), .BX(BX), .CX(CX), .DX(DX), .Out(div2_1_out));
  or or_1 (Overflow, mult_1_overflow, sub_1_overflow, add_1_overflow);
  Multiplexer #(.select(5), .width(8)) multiplexer_1 (
    .in0(add_1_out), .in1(sub_1_out), .in2(mult_1_out), .in3({8{1'b0}}), .in4({8{1'b0}}), .in5({8{1'b0}}),
    .in6({8{1'b0}}), .in7({8{1'b0}}), .in8({8{1'b0}}), .in9({8{1'b0}}), .in10({8{1'b0}}), .in11({8{1'b0}}),
    .in12({8{1'b0}}), .in13({8{1'b0}}), .in14({8{1'b0}}), .in15({8{1'b0}}), .in16({8{1'b0}}),
    .in17({8{1'b0}}), .in18({8{1'b0}}), .in19({8{1'b0}}), .in20({8{1'b0}}), .in21({8{1'b0}}),
    .in22(div2_1_out), .in23({8{1'b0}}), .in24({8{1'b0}}), .in25({8{1'b0}}), .in26({8{1'b0}}),
    .in27({8{1'b0}}), .in28({8{1'b0}}), .in29({8{1'b0}}), .in30({8{1'b0}}), .in31({8{1'b0}}), .out(Out),
    .sel(IR));

  assign Reg = 3'b000;

  // Notes on the sheet:
  //   MUL
  //   SUB
  //   ADD
  //   DIV
endmodule

module CLR (
  input  [4:0] IR,
  input  Store,
  output KillCLK,
  output Clear
);

  wire and_1_out, not_1_out, not_2_out, not_3_out;

  not not_1 (not_1_out, IR[2]);
  not not_2 (not_2_out, IR[3]);
  not not_3 (not_3_out, IR[4]);
  and and_1 (and_1_out, IR[0], IR[1], not_1_out, not_2_out, not_3_out);
  and and_2 (Clear, and_1_out, Store);

  assign KillCLK = Clear;
endmodule

module Counter (
  input  Clock,
  input  Clear,
  output [2:0] out_3
);

  wire and_1_out, and_2_out, j_k_ff_1_qn, j_k_ff_3_qn;

  and and_1 (and_1_out, out_3[1], out_3[0]);
  J_K_Flip_Flop j_k_ff_1 (
    .J(and_1_out), .clk(Clock), .K(out_3[0]), .Q(out_3[2]), .Qn(j_k_ff_1_qn), .reset(Clear));  // open: preset
  and and_2 (and_2_out, j_k_ff_1_qn, out_3[0]);
  J_K_Flip_Flop j_k_ff_2 (.J(and_2_out), .clk(Clock), .K(out_3[0]), .Q(out_3[1]), .reset(Clear));  // open: Qn, preset
  J_K_Flip_Flop j_k_ff_3 (
    .J(j_k_ff_3_qn), .clk(Clock), .K(j_k_ff_1_qn), .Q(out_3[0]), .Qn(j_k_ff_3_qn), .reset(Clear));  // open: preset
endmodule

module Offset (
  output [7:0] out_1
);


  assign out_1 = 8'h1;
endmodule

// RST
module RESET (
  input  [4:0] IR,
  input  Store,
  output KillCLK,
  output out_4
);

  wire and_1_out, not_1_out, not_2_out, not_3_out, not_4_out;

  not not_1 (not_1_out, IR[0]);
  not not_2 (not_2_out, IR[1]);
  not not_3 (not_3_out, IR[3]);
  not not_4 (not_4_out, IR[4]);
  and and_1 (and_1_out, not_1_out, not_2_out, IR[2], not_3_out, not_4_out);
  and and_2 (KillCLK, and_1_out, Store);

  assign out_4 = KillCLK;
endmodule

module JMP (
  input  [7:0] RA,
  input  [7:0] AX,
  input  [7:0] BX,
  input  [7:0] CX,
  input  [7:0] DX,
  input  [4:0] IR,
  input  Execute,
  input  Store,
  output [7:0] CSIn,
  output KillCLK,
  output CSCLK
);

  wire and_1_out, not_1_out, not_2_out, not_3_out, or_1_out;

  Multiplexer #(.select(2), .width(8)) multiplexer_1 (
    .in0(AX), .in1(BX), .in2(CX), .in3(DX), .out(CSIn), .sel(RA[1:0]));
  not not_1 (not_1_out, IR[1]);
  and and_1 (and_1_out, IR[0], not_1_out, IR[2], not_2_out, not_3_out);
  not not_2 (not_2_out, IR[3]);
  not not_3 (not_3_out, IR[4]);
  and and_2 (KillCLK, and_1_out, or_1_out);
  and and_3 (CSCLK, and_1_out, Store);
  or or_1 (or_1_out, Execute, Store);
endmodule

module LJMP (
  input  [7:0] RA,
  input  [7:0] RB,
  input  [7:0] AX,
  input  [7:0] BX,
  input  [7:0] CX,
  input  [7:0] DX,
  input  [4:0] IR,
  input  Execute,
  input  Store,
  output [7:0] CO,
  output [7:0] CS,
  output KillCLK,
  output COCSCLK
);

  wire and_1_out, not_1_out, not_2_out, not_3_out, or_1_out;

  not not_1 (not_1_out, IR[0]);
  not not_2 (not_2_out, IR[3]);
  not not_3 (not_3_out, IR[4]);
  Multiplexer #(.select(2), .width(8)) multiplexer_1 (.in0(AX), .in1(BX), .in2(CX), .in3(DX), .out(CO), .sel(RA[1:0]));
  Multiplexer #(.select(2), .width(8)) multiplexer_2 (.in0(AX), .in1(BX), .in2(CX), .in3(DX), .out(CS), .sel(RB[1:0]));
  and and_1 (and_1_out, not_1_out, IR[1], IR[2], not_2_out, not_3_out);
  and and_2 (KillCLK, and_1_out, or_1_out);
  and and_3 (COCSCLK, and_1_out, Store);
  or or_1 (or_1_out, Execute, Store);
endmodule

module JLP (
  input  [7:0] RA,
  input  [4:0] IR,
  input  Execute,
  input  Store,
  output [7:0] CSIn,
  output KillCLK,
  output CSCLK
);

  wire and_1_out, not_1_out, not_2_out, or_1_out;

  and and_1 (and_1_out, IR[0], IR[1], IR[2], not_1_out, not_2_out);
  not not_1 (not_1_out, IR[3]);
  not not_2 (not_2_out, IR[4]);
  and and_2 (KillCLK, and_1_out, or_1_out);
  and and_3 (CSCLK, and_1_out, Store);
  or or_1 (or_1_out, Execute, Store);

  assign CSIn = RA;
endmodule

module MOV (
  input  [7:0] RA,
  input  [7:0] RB,
  input  [7:0] AX,
  input  [7:0] BX,
  input  [7:0] CX,
  input  [7:0] DX,
  input  [7:0] CO,
  input  [7:0] CS,
  input  [7:0] DS,
  output [2:0] Reg,
  output [7:0] Out
);

  Multiplexer #(.select(3), .width(8)) multiplexer_1 (
    .in0(AX), .in1(BX), .in2(CX), .in3(DX), .in4(CO), .in5(CS), .in6(DS), .out(Out), .sel(RB[2:0]));  // open: in7

  assign Reg = RA[2:0];
endmodule

module MOVL (
  input  [7:0] RA,
  input  [7:0] RB,
  output [2:0] Reg,
  output [7:0] Out
);


  assign Out = RB;
  assign Reg = RA[2:0];
endmodule

module PUSH (
  input  [7:0] SS,
  input  [7:0] RA,
  input  [7:0] AX,
  input  [7:0] BX,
  input  [7:0] CX,
  input  [7:0] DX,
  input  [4:0] IR,
  input  Execute,
  input  Store,
  output [7:0] SSInc,
  output KillClk,
  output [20:0] Data,
  output ERSSCLK,
  output WRI,
  output [1:0] ER
);

  wire and_1_out, not_1_out, not_2_out, not_3_out, or_1_out;

  Multiplexer #(.select(2), .width(8)) multiplexer_1 (
    .in0(AX), .in1(BX), .in2(CX), .in3(DX), .out(Data[7:0]), .sel(RA[1:0]));
  Adder adder_1 (.a(SS), .b(8'h1), .out(SSInc));  // open: cin, cout
  not not_1 (not_1_out, IR[0]);
  not not_2 (not_2_out, IR[1]);
  not not_3 (not_3_out, IR[3]);
  and and_1 (and_1_out, not_1_out, not_2_out, IR[2], not_3_out, IR[4]);
  or or_1 (or_1_out, Store, Execute);
  and and_2 (ERSSCLK, and_1_out, Execute);
  and and_3 (WRI, and_1_out, Store);
  and and_4 (KillClk, and_1_out, or_1_out);

  assign Data[20:8] = {13{1'b0}};
  assign ER = 2'b10;
endmodule

module DIV2 (
  input  [7:0] RA,
  input  [7:0] AX,
  input  [7:0] BX,
  input  [7:0] CX,
  input  [7:0] DX,
  output [7:0] Out
);

  wire [0:0] multiplexer_1_out;

  Multiplexer #(.select(2), .width(8)) multiplexer_1 (
    .in0(AX), .in1(BX), .in2(CX), .in3(DX), .out({Out[6:0], multiplexer_1_out[0]}), .sel(RA[1:0]));
  not not_1 (Out[7], 1'b1);
endmodule

module POP (
  input  [7:0] SS,
  input  [7:0] RA,
  input  [4:0] IR,
  input  Clr,
  input  Execute,
  input  [20:0] Data,
  output [7:0] SSDec,
  output [2:0] Reg,
  output SSCLK,
  output ERCLK,
  output [1:0] ER,
  output [7:0] Out
);

  wire and_1_out, not_1_out, not_2_out;

  not not_1 (not_1_out, IR[1]);
  not not_2 (not_2_out, IR[3]);
  Subtractor subtractor_1 (.a(SS), .b(8'h1), .out(SSDec));  // open: bin, bout
  and and_1 (and_1_out, IR[0], not_1_out, IR[2], not_2_out, IR[4]);
  and and_2 (SSCLK, Clr, and_1_out);
  and and_3 (ERCLK, and_1_out, Execute);

  assign ER = 2'b10;
  assign Out = Data[7:0];
  assign Reg = RA[2:0];
endmodule

module MOVFilter (
  input  CLK,
  input  [4:0] IR,
  output OutCLK
);

  wire and_1_out, and_2_out, not_1_out, not_2_out, not_3_out, not_4_out, not_5_out, or_1_out;

  not not_1 (not_1_out, IR[4]);
  not not_2 (not_2_out, IR[0]);
  not not_3 (not_3_out, IR[1]);
  not not_4 (not_4_out, IR[2]);
  not not_5 (not_5_out, IR[3]);
  and and_1 (and_1_out, IR[0], not_1_out);
  and and_2 (and_2_out, not_2_out, IR[4]);
  or or_1 (or_1_out, and_1_out, and_2_out);
  and and_3 (OutCLK, CLK, or_1_out);
endmodule

module CALL (
  input  [7:0] SS,
  input  [7:0] RA,
  input  [7:0] AX,
  input  [7:0] BX,
  input  [7:0] CX,
  input  [7:0] DX,
  input  [7:0] CS,
  input  [7:0] CO,
  input  [4:0] IR,
  input  Execute,
  input  Store,
  input  Clear,
  output [7:0] SSInc,
  output [7:0] CSIn,
  output [20:0] Data,
  output ERSSCLK,
  output WRI,
  output CSCLK,
  output [1:0] ER,
  output KillClk
);

  wire and_1_out, not_1_out, not_2_out, not_3_out, or_1_out;

  Adder adder_1 (.a(SS), .b(8'h1), .out(SSInc));  // open: cin, cout
  Multiplexer #(.select(2), .width(8)) multiplexer_1 (
    .in0(AX), .in1(BX), .in2(CX), .in3(DX), .out(CSIn), .sel(RA[1:0]));
  not not_1 (not_1_out, IR[1]);
  not not_2 (not_2_out, IR[2]);
  not not_3 (not_3_out, IR[3]);
  and and_1 (and_1_out, IR[0], not_1_out, not_2_out, not_3_out, IR[4]);
  and and_2 (KillClk, and_1_out, or_1_out);
  and and_3 (ERSSCLK, and_1_out, Execute);
  and and_4 (WRI, and_1_out, Store);
  and and_5 (CSCLK, and_1_out, Clear);
  or or_1 (or_1_out, Execute, Store);

  assign Data = {{5{1'b0}}, CO, CS};
  assign ER = 2'b10;
endmodule

module RET (
  input  [7:0] SS,
  input  [4:0] IR,
  input  Clear,
  input  Execute,
  input  Store,
  input  [20:0] Data,
  output [7:0] SSDec,
  output COCSCLK,
  output SSCLK,
  output ERCLK,
  output [1:0] ER,
  output [7:0] CSIn,
  output [7:0] COin,
  output KillClk
);

  wire and_1_out, not_1_out, not_2_out, not_3_out, or_1_out;

  not not_1 (not_1_out, IR[0]);
  not not_2 (not_2_out, IR[2]);
  not not_3 (not_3_out, IR[3]);
  Subtractor subtractor_1 (.a(SS), .b(8'h1), .out(SSDec));  // open: bin, bout
  and and_1 (and_1_out, not_1_out, IR[1], not_2_out, not_3_out, IR[4]);
  and and_2 (KillClk, and_1_out, or_1_out);
  or or_1 (or_1_out, Execute, Store);
  and and_3 (SSCLK, Clear, and_1_out);
  and and_4 (COCSCLK, and_1_out, Store);
  and and_5 (ERCLK, and_1_out, Execute);

  assign COin = Data[15:8];
  assign CSIn = Data[7:0];
  assign ER = 2'b10;
endmodule

module CMP (
  input  [7:0] RA,
  input  [7:0] RB,
  input  [7:0] AX,
  input  [7:0] BX,
  input  [7:0] CX,
  input  [7:0] DX,
  input  [4:0] IR,
  input  Execute,
  input  Store,
  output GT,
  output EQ,
  output LT,
  output FRCLK,
  output KillClk
);

  wire and_1_out, not_1_out, not_2_out, or_1_out;
  wire [7:0] multiplexer_1_out, multiplexer_2_out;

  not not_1 (not_1_out, IR[2]);
  not not_2 (not_2_out, IR[3]);
  Multiplexer #(.select(2), .width(8)) multiplexer_1 (
    .in0(AX), .in1(BX), .in2(CX), .in3(DX), .out(multiplexer_1_out), .sel(RA[1:0]));
  Multiplexer #(.select(2), .width(8)) multiplexer_2 (
    .in0(AX), .in1(BX), .in2(CX), .in3(DX), .out(multiplexer_2_out), .sel(RB[1:0]));
  and and_1 (and_1_out, IR[0], IR[1], not_1_out, not_2_out, IR[4]);
  and and_2 (FRCLK, and_1_out, Execute);
  or or_1 (or_1_out, Store, Execute);
  and and_3 (KillClk, and_1_out, or_1_out);
  Comparator #(.mode("unsigned")) comparator_1 (
    .a(multiplexer_1_out), .b(multiplexer_2_out), .gt(GT), .eq(EQ), .lt(LT));
endmodule

module CJMP (
  input  GT,
  input  EQ,
  input  LT,
  input  [7:0] BX,
  input  [4:0] IR,
  input  ZF,
  input  Execute,
  input  Store,
  output [7:0] CSIn,
  output KillCLK,
  output CSCLK
);

  wire and_1_out, and_2_out, and_3_out, and_4_out, and_5_out, and_6_out, and_7_out, and_8_out, and_9_out,
       and_10_out, and_11_out, and_12_out, and_13_out, and_14_out, and_15_out, and_16_out, and_17_out,
       and_18_out, and_19_out, and_20_out, and_21_out, JE_out, JG_out, JGE_out, JL_out, JLE_out, JNZ_out,
       JZ_out, not_1_out, not_2_out, not_3_out, not_4_out, not_5_out, not_6_out, not_7_out, not_8_out,
       not_9_out, not_10_out, not_11_out, not_12_out, not_13_out, not_14_out, not_15_out, not_16_out,
       not_17_out, not_18_out, not_19_out, not_20_out, or_1_out, or_2_out, or_3_out, or_4_out, or_6_out,
       or_7_out, or_8_out;

  not not_1 (not_1_out, IR[0]);
  not not_2 (not_2_out, IR[1]);
  not not_3 (not_3_out, IR[2]);
  not not_4 (not_4_out, IR[4]);
  not not_5 (not_5_out, IR[1]);
  not not_6 (not_6_out, IR[2]);
  not not_7 (not_7_out, IR[4]);
  not not_8 (not_8_out, IR[0]);
  not not_9 (not_9_out, IR[2]);
  not not_10 (not_10_out, IR[4]);
  not not_11 (not_11_out, IR[2]);
  not not_12 (not_12_out, IR[4]);
  not not_13 (not_13_out, IR[0]);
  not not_14 (not_14_out, IR[1]);
  not not_15 (not_15_out, IR[4]);
  not not_16 (not_16_out, IR[1]);
  not not_17 (not_17_out, IR[4]);
  not not_18 (not_18_out, IR[0]);
  not not_19 (not_19_out, IR[4]);
  and JG (JG_out, not_1_out, not_2_out, not_3_out, IR[3], not_4_out);
  and JGE (JGE_out, IR[0], not_5_out, not_6_out, IR[3], not_7_out);
  and JL (JL_out, not_8_out, IR[1], not_9_out, IR[3], not_10_out);
  and JLE (JLE_out, IR[0], IR[1], not_11_out, IR[3], not_12_out);
  and JE (JE_out, not_13_out, not_14_out, IR[2], IR[3], not_15_out);
  and JZ (JZ_out, IR[0], not_16_out, IR[2], IR[3], not_17_out);
  and JNZ (JNZ_out, not_18_out, IR[1], IR[2], IR[3], not_19_out);
  and and_1 (and_1_out, JG_out, Store);
  and and_2 (and_2_out, JGE_out, or_1_out);
  and and_3 (and_3_out, JGE_out, Store);
  or or_1 (or_1_out, Execute, Store);
  and and_4 (and_4_out, JL_out, Store);
  and and_5 (and_5_out, JLE_out, or_2_out);
  and and_6 (and_6_out, JLE_out, Store);
  or or_2 (or_2_out, Execute, Store);
  and and_7 (and_7_out, JE_out, Store);
  and and_8 (and_8_out, JZ_out, or_3_out);
  and and_9 (and_9_out, JZ_out, Store);
  or or_3 (or_3_out, Execute, Store);
  and and_10 (and_10_out, JNZ_out, or_4_out);
  and and_11 (and_11_out, JNZ_out, Store);
  or or_4 (or_4_out, Execute, Store);
  or or_5 (KillCLK, and_12_out, and_2_out, and_13_out, and_5_out, and_14_out, and_8_out, and_10_out);
  and and_12 (and_12_out, JG_out, or_6_out);
  or or_6 (or_6_out, Execute, Store);
  and and_13 (and_13_out, JL_out, or_7_out);
  or or_7 (or_7_out, Execute, Store);
  and and_14 (and_14_out, JE_out, or_8_out);
  or or_8 (or_8_out, Execute, Store);
  and and_15 (and_15_out, LT, and_4_out);
  and and_16 (and_16_out, GT, and_1_out);
  and and_17 (and_17_out, and_3_out, GT, EQ);
  and and_18 (and_18_out, EQ, LT, and_6_out);
  and and_19 (and_19_out, and_9_out, ZF);
  not not_20 (not_20_out, ZF);
  and and_20 (and_20_out, not_20_out, and_11_out);
  and and_21 (and_21_out, EQ, and_7_out);
  or or_9 (CSCLK, and_16_out, and_17_out, and_15_out, and_18_out, and_21_out, and_19_out, and_20_out);

  assign CSIn = BX;
endmodule

module MMIV (
  input  [7:0] RA,
  input  [7:0] RB,
  input  [7:0] AX,
  input  [7:0] BX,
  input  [7:0] CX,
  input  [7:0] DX,
  input  [4:0] IR,
  input  Execute,
  input  Store,
  output [7:0] DSIn,
  output [20:0] Data,
  output ERDSCLK,
  output WRI,
  output [1:0] ER,
  output KillClk
);

  wire and_1_out, not_1_out, or_1_out;

  Multiplexer #(.select(2), .width(8)) multiplexer_1 (
    .in0(AX), .in1(BX), .in2(CX), .in3(DX), .out(Data[7:0]), .sel(RB[1:0]));
  not not_1 (not_1_out, IR[3]);
  and and_1 (and_1_out, IR[0], IR[1], IR[2], not_1_out, IR[4]);
  not not_2 (Data[20], 1'b1);
  and and_2 (ERDSCLK, and_1_out, Execute);
  and and_3 (WRI, and_1_out, Store);
  or or_1 (or_1_out, Execute, Store);
  and and_4 (KillClk, and_1_out, or_1_out);

  assign Data[19:8] = {12{Data[20]}};
  assign DSIn = RA;
  assign ER = 2'b01;
endmodule

// DS
module DataOffset (
  output [7:0] out_1
);


  assign out_1 = 8'hfe;
endmodule

module MMOV (
  input  [7:0] RA,
  input  [7:0] RB,
  input  [4:0] IR,
  input  Execute,
  input  [20:0] Data,
  output [2:0] Reg,
  output [7:0] DSIn,
  output DSERCLK,
  output [1:0] ER,
  output [7:0] Out
);

  wire and_1_out, not_1_out, not_2_out, not_3_out;

  not not_1 (not_1_out, IR[0]);
  not not_2 (not_2_out, IR[1]);
  not not_3 (not_3_out, IR[2]);
  and and_1 (and_1_out, not_1_out, not_2_out, not_3_out, IR[3], IR[4]);
  and and_2 (DSERCLK, Execute, and_1_out);

  assign DSIn = RB;
  assign ER = 2'b01;
  assign Out = Data[7:0];
  assign Reg = RA[2:0];
endmodule

module CU (
  input  [4:0] IR,
  input  [7:0] RA,
  input  [7:0] RB,
  input  [7:0] AX,
  input  [7:0] BX,
  input  [7:0] CX,
  input  [7:0] DX,
  input  [7:0] CO,
  input  [7:0] CS,
  input  [7:0] DS,
  input  CSCLKSTORMUX5,
  input  [7:0] SS,
  input  COCLKSTORMUX4,
  input  CSCLKSTORMUX6,
  input  [20:0] Data,
  input  Decode,
  input  in_17,
  input  EQ,
  input  in_19,
  input  ZF,
  input  Execute,
  input  Store,
  input  Clear,
  output CSCLK,
  output COCLK,
  output DSCLK,
  output SSCLK,
  output ERCLK,
  output KillCLK,
  output WRI,
  output ERCLR,
  output Overflow,
  output [7:0] CSIn,
  output [7:0] DSIn,
  output [1:0] ER,
  output [7:0] Out,
  output FRCLK,
  output [2:0] Reg,
  output GT,
  output out_40,
  output LT,
  output out_42,
  output [20:0] out_43,
  output RST,
  output [7:0] SSIn,
  output [7:0] COIn
);

  wire call_1_csclk, call_1_erssclk, call_1_killclk, call_1_wri, cjmp_1_csclk, cjmp_1_killclk, clr_1_clear,
       clr_1_killclk, cmp_1_killclk, jlp_1_csclk, jlp_1_killclk, jmp_1_csclk, jmp_1_killclk, ljmp_1_cocsclk,
       ljmp_1_killclk, mmiv_1_erdsclk, mmiv_1_killclk, mmiv_1_wri, mmov_1_dserclk, or_1_out, or_2_out,
       pop_1_erclk, pop_1_ssclk, push_1_erssclk, push_1_killclk, push_1_wri, reset_1_killclk, ret_1_cocsclk,
       ret_1_erclk, ret_1_killclk, ret_1_ssclk;
  wire [1:0] call_1_er, mmiv_1_er, mmov_1_er, pop_1_er, push_1_er, ret_1_er;
  wire [2:0] alu_1_reg, mmov_1_reg, mov_1_reg, movl_1_reg, msk_1_reg, mskb_1_reg, pop_1_reg;
  wire [7:0] alu_1_out, call_1_csin, call_1_ssinc, cjmp_1_csin, jlp_1_csin, jmp_1_csin, ljmp_1_co, ljmp_1_cs,
       mmiv_1_dsin, mmov_1_dsin, mmov_1_out, mov_1_out, movl_1_out, msk_1_out, mskb_1_out, pop_1_out,
       pop_1_ssdec, push_1_ssinc, ret_1_coin, ret_1_csin, ret_1_ssdec;
  wire [20:0] call_1_data, mmiv_1_data, push_1_data;

  or or_1 (or_1_out, or_2_out, ret_1_killclk, mmiv_1_killclk);
  or or_2 (or_2_out, call_1_killclk, cmp_1_killclk);
  or or_3 (KillCLK, jlp_1_killclk, clr_1_killclk, reset_1_killclk, jmp_1_killclk, ljmp_1_killclk, push_1_killclk, or_1_out, cjmp_1_killclk);
  ALU alu_1 (
    .IR(IR), .AX(AX), .BX(BX), .CX(CX), .DX(DX), .RA(RA), .Overflow(Overflow), .Out(alu_1_out),
    .Reg(alu_1_reg));
  RET ret_1 (
    .SS(SS), .IR(IR), .Data(Data), .KillClk(ret_1_killclk), .Clear(Clear), .Execute(Execute), .Store(Store),
    .SSDec(ret_1_ssdec), .COCSCLK(ret_1_cocsclk), .SSCLK(ret_1_ssclk), .ERCLK(ret_1_erclk), .ER(ret_1_er),
    .CSIn(ret_1_csin), .COin(ret_1_coin));
  MMIV mmiv_1 (
    .RA(RA), .RB(RB), .AX(AX), .BX(BX), .CX(CX), .DX(DX), .IR(IR), .KillClk(mmiv_1_killclk),
    .Execute(Execute), .Store(Store), .DSIn(mmiv_1_dsin), .Data(mmiv_1_data), .ERDSCLK(mmiv_1_erdsclk),
    .WRI(mmiv_1_wri), .ER(mmiv_1_er));
  JMP jmp_1 (
    .RA(RA), .AX(AX), .BX(BX), .CX(CX), .DX(DX), .IR(IR), .KillCLK(jmp_1_killclk), .Execute(Execute),
    .Store(Store), .CSIn(jmp_1_csin), .CSCLK(jmp_1_csclk));
  POP pop_1 (
    .SS(SS), .RA(RA), .IR(IR), .Data(Data), .Clr(Clear), .Execute(Execute), .SSDec(pop_1_ssdec),
    .Reg(pop_1_reg), .SSCLK(pop_1_ssclk), .ERCLK(pop_1_erclk), .ER(pop_1_er), .Out(pop_1_out));
  PUSH push_1 (
    .SS(SS), .RA(RA), .AX(AX), .BX(BX), .CX(CX), .DX(DX), .IR(IR), .KillClk(push_1_killclk),
    .Execute(Execute), .Store(Store), .SSInc(push_1_ssinc), .Data(push_1_data), .ERSSCLK(push_1_erssclk),
    .WRI(push_1_wri), .ER(push_1_er));
  MOV mov_1 (
    .RA(RA), .RB(RB), .AX(AX), .BX(BX), .CX(CX), .DX(DX), .CO(CO), .CS(CS), .DS(DS), .Reg(mov_1_reg),
    .Out(mov_1_out));
  CALL call_1 (
    .SS(SS), .RA(RA), .AX(AX), .BX(BX), .CX(CX), .DX(DX), .CS(CS), .CO(CO), .IR(IR),
    .KillClk(call_1_killclk), .Execute(Execute), .Store(Store), .Clear(Clear), .SSInc(call_1_ssinc),
    .CSIn(call_1_csin), .Data(call_1_data), .ERSSCLK(call_1_erssclk), .WRI(call_1_wri), .CSCLK(call_1_csclk),
    .ER(call_1_er));
  CJMP cjmp_1 (
    .GT(in_17), .EQ(EQ), .LT(in_19), .BX(BX), .IR(IR), .ZF(ZF), .KillCLK(cjmp_1_killclk), .Execute(Execute),
    .Store(Store), .CSIn(cjmp_1_csin), .CSCLK(cjmp_1_csclk));
  CMP cmp_1 (
    .RA(RA), .RB(RB), .AX(AX), .BX(BX), .CX(CX), .DX(DX), .IR(IR), .KillClk(cmp_1_killclk), .GT(GT),
    .EQ(out_40), .LT(LT), .Execute(Execute), .Store(Store), .FRCLK(FRCLK));
  LJMP ljmp_1 (
    .RA(RA), .RB(RB), .AX(AX), .BX(BX), .CX(CX), .DX(DX), .IR(IR), .KillCLK(ljmp_1_killclk),
    .Execute(Execute), .Store(Store), .CO(ljmp_1_co), .CS(ljmp_1_cs), .COCSCLK(ljmp_1_cocsclk));
  MMOV mmov_1 (
    .RA(RA), .RB(RB), .IR(IR), .Data(Data), .Execute(Execute), .Reg(mmov_1_reg), .DSIn(mmov_1_dsin),
    .DSERCLK(mmov_1_dserclk), .ER(mmov_1_er), .Out(mmov_1_out));
  CLR clr_1 (.IR(IR), .KillCLK(clr_1_killclk), .Store(Store), .Clear(clr_1_clear));
  MOVL movl_1 (.RA(RA), .RB(RB), .Reg(movl_1_reg), .Out(movl_1_out));
  JLP jlp_1 (
    .RA(RA), .IR(IR), .KillCLK(jlp_1_killclk), .Execute(Execute), .Store(Store), .CSIn(jlp_1_csin),
    .CSCLK(jlp_1_csclk));
  RESET reset_1 (.IR(IR), .KillCLK(reset_1_killclk), .Store(Store), .out_4(RST));
  MSK msk_1 (.AX(AX), .DX(DX), .BX(BX), .Reg(msk_1_reg), .Out(msk_1_out));
  MSKB mskb_1 (.DX(DX), .BX(BX), .Reg(mskb_1_reg), .Out(mskb_1_out));
  or or_4 (CSCLK, Decode, jlp_1_csclk, cjmp_1_csclk, call_1_csclk, jmp_1_csclk, ret_1_cocsclk, ljmp_1_cocsclk, CSCLKSTORMUX5);
  or or_5 (COCLK, ret_1_cocsclk, ljmp_1_cocsclk, COCLKSTORMUX4);
  or or_6 (DSCLK, CSCLKSTORMUX6, mmov_1_dserclk, mmiv_1_erdsclk);
  or or_7 (SSCLK, call_1_erssclk, push_1_erssclk, pop_1_ssclk, ret_1_ssclk);
  or or_8 (out_42, clr_1_clear, RST);
  or or_9 (ERCLK, mmov_1_dserclk, call_1_erssclk, push_1_erssclk, pop_1_erclk, mmiv_1_erdsclk, ret_1_erclk);
  or or_10 (WRI, mmiv_1_wri, push_1_wri, call_1_wri);
  Multiplexer #(.select(5), .width(2)) multiplexer_1 (
    .in17(call_1_er), .in18(ret_1_er), .in20(push_1_er), .in21(pop_1_er), .in23(mmiv_1_er), .in24(mmov_1_er),
    .out(ER), .sel(IR));  // open: in0, in1, in2, in3, in4, in5, in6, in7, in8, in9, in10, in11, in12, in13, in14, in15, in16, in19, in22, in25, in26, in27, in28, in29, in30, in31
  Multiplexer #(.select(5), .width(8)) multiplexer_2 (
    .in0(alu_1_out), .in1(alu_1_out), .in2(alu_1_out), .in15(mov_1_out), .in16(movl_1_out), .in21(pop_1_out),
    .in22(alu_1_out), .in24(mmov_1_out), .in26(msk_1_out), .in27(mskb_1_out), .out(Out), .sel(IR));  // open: in3, in4, in5, in6, in7, in8, in9, in10, in11, in12, in13, in14, in17, in18, in19, in20, in23, in25, in28, in29, in30, in31
  Multiplexer #(.select(5), .width(3)) multiplexer_3 (
    .in0(alu_1_reg), .in1(alu_1_reg), .in2(alu_1_reg), .in3(3'b000), .in4(3'b000), .in5(3'b000),
    .in6(3'b000), .in7(3'b000), .in8(3'b000), .in9(3'b000), .in10(3'b000), .in11(3'b000), .in12(3'b000),
    .in13(3'b000), .in14(3'b000), .in15(mov_1_reg), .in16(movl_1_reg), .in17(3'b000), .in18(3'b000),
    .in19(3'b000), .in20(3'b000), .in21(pop_1_reg), .in22(alu_1_reg), .in23(3'b000), .in24(mmov_1_reg),
    .in25(3'b000), .in26(msk_1_reg), .in27(mskb_1_reg), .in28(3'b000), .in29(3'b000), .in30(3'b000),
    .in31(3'b000), .out(Reg), .sel(IR));
  Multiplexer #(.select(5), .width(21)) multiplexer_4 (
    .in17(call_1_data), .in20(push_1_data), .in23(mmiv_1_data), .out(out_43), .sel(IR));  // open: in0, in1, in2, in3, in4, in5, in6, in7, in8, in9, in10, in11, in12, in13, in14, in15, in16, in18, in19, in21, in22, in24, in25, in26, in27, in28, in29, in30, in31
  Multiplexer #(.select(5), .width(8)) multiplexer_5 (
    .in17(call_1_ssinc), .in18(ret_1_ssdec), .in20(push_1_ssinc), .in21(pop_1_ssdec), .out(SSIn), .sel(IR));  // open: in0, in1, in2, in3, in4, in5, in6, in7, in8, in9, in10, in11, in12, in13, in14, in15, in16, in19, in22, in23, in24, in25, in26, in27, in28, in29, in30, in31
  Multiplexer #(.select(5), .width(8)) multiplexer_6 (
    .in0(CSIn), .in1(CSIn), .in2(CSIn), .in3(CSIn), .in4(CSIn), .in5(CSIn), .in6(ljmp_1_co), .in7(CSIn),
    .in8(CSIn), .in9(CSIn), .in10(CSIn), .in11(CSIn), .in12(CSIn), .in13(CSIn), .in14(CSIn), .in15(CSIn),
    .in16(CSIn), .in17(CSIn), .in18(ret_1_coin), .in19(CSIn), .in20(CSIn), .in21(CSIn), .in22(CSIn),
    .in23(CSIn), .in24(CSIn), .in25(CSIn), .in26(CSIn), .in27(CSIn), .in28(CSIn), .in29(CSIn), .in30(CSIn),
    .in31(CSIn), .out(COIn), .sel(IR));
  Multiplexer #(.select(5), .width(8)) multiplexer_7 (
    .in0({8{1'b0}}), .in1({8{1'b0}}), .in2({8{1'b0}}), .in3({8{1'b0}}), .in4({8{1'b0}}), .in5(jmp_1_csin),
    .in6(ljmp_1_cs), .in7(jlp_1_csin), .in8(cjmp_1_csin), .in9(cjmp_1_csin), .in10(cjmp_1_csin),
    .in11(cjmp_1_csin), .in12(cjmp_1_csin), .in13(cjmp_1_csin), .in14(cjmp_1_csin), .in15(Out), .in16(Out),
    .in17(call_1_csin), .in18(ret_1_csin), .in19({8{1'b0}}), .in20({8{1'b0}}), .in21({8{1'b0}}),
    .in22({8{1'b0}}), .in23(mmiv_1_dsin), .in24(mmov_1_dsin), .in25({8{1'b0}}), .in26({8{1'b0}}),
    .in27({8{1'b0}}), .in28({8{1'b0}}), .in29({8{1'b0}}), .in30({8{1'b0}}), .in31({8{1'b0}}), .out(CSIn),
    .sel(IR));

  assign DSIn = CSIn;
  assign ERCLR = Clear;
endmodule

module NETWORK_IN_65bb84dc (
  input  [7:0] NETWORK_CTRL_15d682f0,
  output [7:0] OUT
);

  wire [15:0] counter_1_q;

  Counter_part #(.max('hffff), .width(16)) counter_1 (
    .Q(counter_1_q), .clk(NETWORK_CTRL_15d682f0[2]), .clr(NETWORK_CTRL_15d682f0[3]));  // open: load, D, count, carry, up
  ROM #(.addrWidth(16)) rom_1 (.addr(counter_1_q), .data(OUT));

  // Notes on the sheet:
  //   CTS
  //   contents of rom_1 (hex, n*v repeats v):
  //   ac c2 50 a4 fe 79 54 2a 19 5c d1 45 64 37 7c c5 e3 ef 0 a0 9e 1 71 d 22 32 cc 47 bf 16 1d 2e 1b 5f
  //   95 95 2a 16 34 81 e1 78 76 7e f7 aa 12 c2 11 b7 2d 15 14 4c 76 3a 1b 47 f2 f9 41 24 ba 13 cf b7 e4
  //   ff 25 49 9c 3c 52 87 f8 bb 6f 5d 1d 30 28 56 a2 25 ff 1c 48 5c 71 f5 c3 b7 bf 4e 87 29 b6 30 68 95
  //   b2 2a 17 12 21 c6 77 fc fc 30 44 22 d4 22 3b b1 b0 2 88 ce 2a f5 c5 23 dd c3 9f bf 63 31 35 30 2e 94
  //   34 3f 59 91 a3 2e ca 72 7 67 7b fe 60 28 1f bd 60 82 e0 97 97 55 bb 6b a2 c6 62 32 b3 9a ed c5 a4 46
  //   a9 6a 5e 56 b4 5e ed 95 48 5b 71 d6 2b c9 89 8 f7 18 40 a5 2 80 60 1 4 2 18 41 8 4 12 a0 20 44 9 92
  //   34 8b 40 2 20 4 c9 10 1 98 22 44 40 4 a1 10 a 40 5 10 80 20 a 48 4 10 22 81 80 8 20 3 54 84 8 60 2 1
  //   10 8a 20 45 10 a0 4 8 40 11 2 20 53 4 80 8 80 40 1e 1 20 20 18 5 40 82 8 4 12 40 20 1 80 b0 1 4 2 40
  //   8 5 8 2 d0 20 2 4 9 a0 50 80 20 2 1 10 40 8 4 2d 90 42 40 a5 8 2 10 4 11 2 60 8 80 10 2 9 20 c0 4 82
  //   60 10 4 8 1 1 20 d8 2 4 40 80 35 8 2 61 4 80 2 8 10 39 80 44 2 8 5 30 80 42 2 5c 1 20 80 dc a4 db ce
  //   c4
  //   RST
endmodule

module PARALLEL_OUT_2402ca5c (
  input  [7:0] D,
  input  [7:0] CTRL,
  output [7:0] Data,
  output CLK,
  output RESET
);


  assign CLK = CTRL[0];
  assign Data = D;
  assign RESET = CTRL[1];
endmodule

module DX_SELECT_360570a6 (
  input  [7:0] CU,
  input  [7:0] NW,
  input  [7:0] BX,
  output [7:0] DX
);

  Multiplexer #(.enable("true"), .width(8)) multiplexer_1 (.in0(CU), .in1(NW), .out(DX), .sel(BX[0]));  // open: en
endmodule

module MSK (
  input  [7:0] AX,
  input  [7:0] DX,
  input  [7:0] BX,
  output [2:0] Reg,
  output [7:0] Out
);

  wire [7:0] and_1_out;

  assign and_1_out = AX & DX;  // AND_Gate and_1, 8 bits wide
  assign Out = and_1_out | BX;  // OR_Gate or_1, 8 bits wide

  assign Reg = 3'b001;
endmodule

module MSKB (
  input  [7:0] DX,
  input  [7:0] BX,
  output [2:0] Reg,
  output [7:0] Out
);

  assign Out = DX | BX;  // OR_Gate or_1, 8 bits wide

  assign Reg = 3'b001;
endmodule
